// Logisim project TinyCPU-Peripherals.circ as structural Verilog: 3 circuits, main circuit TinyCPUSystemMain
module TinyCPUSystemMain (
  input  CLK,
  input  RESET,
  input  INTERRUPT_REQUEST,
  output [15:0] OUTPUT_PORT_VALUE,
  output OUTPUT_PORT_VALID,
  output INTERRUPT_ENABLED,
  output INTERRUPT_PENDING,
  output IN_INTERRUPT_HANDLER,
  output [11:0] RETURN_ADDRESS,
  output RETURN_ADDRESS_VALID
);
endmodule

module OutputPort (
  input  [15:0] WRITE_VALUE,
  input  WRITE_VALID,
  input  WRITE_ENABLE,
  input  CLK,
  input  RESET,
  output [15:0] VALUE,
  output VALID
);

  Register #(.width(16)) OUTPUT_VALUE (.D(WRITE_VALUE), .en(WRITE_ENABLE), .clk(CLK), .Q(VALUE), .clr(RESET));
  Register #(.width(1)) OUTPUT_VALID (.D(WRITE_VALID), .en(WRITE_ENABLE), .clk(CLK), .Q(VALID), .clr(RESET));

  // Notes on the sheet:
  //   AP-18 output port: value and validity are written atomically; reset clears both registers
endmodule

module OutputMemoryPath (
  input  [11:0] ADDRESS,
  input  [15:0] WRITE_VALUE,
  input  WRITE_VALID,
  input  WRITE_ENABLE,
  input  [15:0] RAM_READ_VALUE,
  input  RAM_READ_VALID,
  input  CLK,
  input  RESET,
  output [15:0] READ_VALUE,
  output READ_VALID,
  output RAM_WRITE_ENABLE,
  output [15:0] OUTPUT_PORT_VALUE,
  output OUTPUT_PORT_VALID
);

  wire undriven;

  Comparator #(.width(12)) OUTPUT_ADDRESS_DECODE ();  // open: a, b, gt, eq, lt
  // NOT_Gate NOT_OUTPUT_ADDRESS is placed but not wired
  // AND_Gate RAM_WRITE_GATE has open pins: in1=undriven, out=open
  // AND_Gate OUTPUT_WRITE_GATE has open pins: in0=undriven, out=open
  Multiplexer #(.width(16)) OUTPUT_READ_VALUE_SELECT ();  // open: in0, in1, out, sel
  Multiplexer OUTPUT_READ_VALID_SELECT ();  // open: in0, in1, out, sel
  OutputPort OUTPUT_PORT ();  // open: WRITE_VALUE, WRITE_VALID, WRITE_ENABLE, CLK, RESET, VALUE, VALID

  // Notes on the sheet:
  //   AP-18 address 0xfff bypasses RAM writes and selects the clocked output port for reads
endmodule
